// Logisim project A2_group3.circ as structural Verilog: 3 circuits, main circuit main
module main (
  input  [2:0] in_1,
  input  [3:0] A,
  input  [3:0] B,
  output [3:0] F3_F2_F1_F0,
  output [3:0] C_S_V_Z
);

  _4_BIT_ALU _4_BIT_ALU (.A(A), .B(B), .in_1(in_1), .F3_F2_F1_F(F3_F2_F1_F0), .C_S_V_Z(C_S_V_Z));

  // Notes on the sheet:
  //   CS2 CS1 CS0
endmodule

module A_modification (
  input  A,
  input  B,
  input  in_3,
  input  CS0,
  input  CS1,
  input  in_6,
  output X
);

  wire and_1_out, and_2_out;

  and and_1 (and_1_out, B, in_3, CS0);
  and and_2 (and_2_out, CS1, in_6);
  or or_1 (X, A, and_1_out, and_2_out);

  // Notes on the sheet:
  //   B! * CS0!
  //   CS1
endmodule

module _4_BIT_ALU (
  input  [2:0] in_1,
  input  [3:0] A,
  input  [3:0] B,
  output [3:0] F3_F2_F1_F,
  output [3:0] C_S_V_Z
);

  wire adder_1_cout, adder_2_cout, adder_3_cout, adder_4_cout, and_1_out, and_2_out, and_3_out, and_4_out,
       and_5_out, and_6_out, and_7_out, and_8_out, and_9_out, and_10_out, and_11_out, and_12_out, and_13_out,
       and_14_out, and_15_out, and_16_out, not_1_out, not_2_out, not_3_out, not_4_out, not_5_out, not_6_out,
       or_1_out, or_2_out, or_3_out, or_4_out;

  not not_1 (not_1_out, B[0]);
  not not_2 (not_2_out, B[1]);
  not not_3 (not_3_out, B[2]);
  not not_4 (not_4_out, B[3]);
  not not_5 (not_5_out, in_1[1]);
  not not_6 (not_6_out, in_1[0]);
  and and_1 (and_1_out, not_1_out, not_6_out);
  and and_2 (and_2_out, not_2_out, not_6_out);
  and and_3 (and_3_out, not_3_out, not_6_out);
  and and_4 (and_4_out, not_4_out, not_6_out);
  and and_5 (and_5_out, B[0], in_1[1], in_1[0]);
  and and_6 (and_6_out, in_1[1], and_1_out);
  and and_7 (and_7_out, B[1], in_1[1], in_1[0]);
  and and_8 (and_8_out, in_1[1], and_2_out);
  and and_9 (and_9_out, B[2], in_1[1], in_1[0]);
  and and_10 (and_10_out, in_1[1], and_3_out);
  and and_11 (and_11_out, B[3], in_1[1], in_1[0]);
  and and_12 (and_12_out, in_1[1], and_4_out);
  or or_1 (or_1_out, A[0], and_5_out, and_6_out);
  or or_2 (or_2_out, A[1], and_7_out, and_8_out);
  or or_3 (or_3_out, A[2], and_9_out, and_10_out);
  or or_4 (or_4_out, A[3], and_11_out, and_12_out);
  and and_13 (and_13_out, not_5_out, in_1[2]);
  Adder #(.width(1)) adder_1 (.a(or_1_out), .b(and_1_out), .out(F3_F2_F1_F[0]), .cin(and_13_out), .cout(adder_1_cout));
  and and_14 (and_14_out, not_5_out, adder_1_cout);
  Adder #(.width(1)) adder_2 (.a(or_2_out), .b(and_2_out), .out(F3_F2_F1_F[1]), .cin(and_14_out), .cout(adder_2_cout));
  and and_15 (and_15_out, not_5_out, adder_2_cout);
  Adder #(.width(1)) adder_3 (.a(or_3_out), .b(and_3_out), .out(F3_F2_F1_F[2]), .cin(and_15_out), .cout(adder_3_cout));
  and and_16 (and_16_out, not_5_out, adder_3_cout);
  and and_17 (C_S_V_Z[3], not_5_out, adder_4_cout);
  Adder #(.width(1)) adder_4 (.a(or_4_out), .b(and_4_out), .out(C_S_V_Z[2]), .cin(and_16_out), .cout(adder_4_cout));
  xor xor_1 (C_S_V_Z[1], and_16_out, C_S_V_Z[3]);
  nor nor_1 (C_S_V_Z[0], F3_F2_F1_F[0], F3_F2_F1_F[1], F3_F2_F1_F[2], C_S_V_Z[2]);

  assign F3_F2_F1_F[3] = C_S_V_Z[2];

  // Notes on the sheet:
  //   B0
  //   B2
  //   B3
  //   !B0
  //   B1
  //   B0
  //   !B1
  //   B3
  //   B1
  //   !B2
  //   !B3
  //   CS2 CS1 CS0
  //   A0
  //   A1
  //   A2
  //   A3
  //   B2
  //   CS2
  //   CS1
  //   CS2
  //   CS1
  //   CS0
  //   !CS1
  //   CS0
  //   !CS0
  //   Y0
  //   A1
  //   Y1
  //   Y2
  //   Y3
  //   X0
  //   X1
  //   X2
  //   X3
  //   Cout
  //   Xi = Ai + Bi * CS1 * CS0 + CS1 * (Bi!) * (CS0!)
  //   Yi = Bi! * CS0!
  //    Zi = CS1! * Ci
endmodule
