// Logisim project 8bitreg-circuit.circ as structural Verilog: 2 circuits, main circuit main
module main (
  input  [3:0] read_reg1,
  input  [3:0] read_reg2,
  input  [3:0] write_reg,
  input  [7:0] write_data,
  output [7:0] out_5,
  output [7:0] out_6
);

  _8_bit_register u_8_bit_register_1 (
    .read_reg1(read_reg1), .read_reg2(read_reg2), .write_reg(write_reg), .write_date(write_data),
    .out_7(out_5), .out_8(out_6));  // open: reg_write, clock
endmodule

// 8-bit reg
module _8_bit_register (
  input  [3:0] read_reg1,
  input  [3:0] read_reg2,
  input  [3:0] write_reg,
  input  [7:0] write_date,
  input  reg_write,
  input  clock,
  output [7:0] out_7,
  output [7:0] out_8
);

  wire and_1_out, and_2_out, and_3_out, and_4_out, and_5_out, and_6_out, and_7_out, and_8_out,
       decoder_1_out0, decoder_1_out1, decoder_1_out2, decoder_1_out3, decoder_1_out4, decoder_1_out5,
       decoder_1_out6, decoder_1_out7;
  wire [7:0] register_1_q, register_2_q, register_3_q, register_4_q, register_5_q, register_6_q,
       register_7_q, register_8_q;

  Decoder #(.select(3)) decoder_1 (
    .out0(decoder_1_out0), .out1(decoder_1_out1), .out2(decoder_1_out2), .out3(decoder_1_out3),
    .out4(decoder_1_out4), .out5(decoder_1_out5), .out6(decoder_1_out6), .out7(decoder_1_out7),
    .sel(write_reg[3:1]));  // open: en
  and and_1 (and_1_out, decoder_1_out0, reg_write);
  and and_2 (and_2_out, decoder_1_out1, reg_write);
  and and_3 (and_3_out, decoder_1_out2, reg_write);
  and and_4 (and_4_out, decoder_1_out3, reg_write);
  and and_5 (and_5_out, decoder_1_out4, reg_write);
  and and_6 (and_6_out, decoder_1_out5, reg_write);
  and and_7 (and_7_out, decoder_1_out6, reg_write);
  and and_8 (and_8_out, decoder_1_out7, reg_write);
  Register register_1 (.D({8{1'b0}}), .Q(register_1_q), .clk(clock), .clr(and_1_out));  // open: en
  Register register_2 (.D(write_date), .Q(register_2_q), .clk(clock), .clr(and_2_out));  // open: en
  Register register_3 (.D(write_date), .Q(register_3_q), .clk(clock), .clr(and_3_out));  // open: en
  Register register_4 (.D(write_date), .Q(register_4_q), .clk(clock), .clr(and_4_out));  // open: en
  Register register_5 (.D(write_date), .Q(register_5_q), .clk(clock), .clr(and_5_out));  // open: en
  Register register_6 (.D(write_date), .Q(register_6_q), .clk(clock), .clr(and_6_out));  // open: en
  Register register_7 (.D(write_date), .Q(register_7_q), .clk(clock), .clr(and_7_out));  // open: en
  Register register_8 (.D(write_date), .Q(register_8_q), .clk(clock), .clr(and_8_out));  // open: en
  Multiplexer #(.select(3), .width(8)) multiplexer_1 (
    .in0(register_1_q), .in1(register_2_q), .in2(register_3_q), .in3(register_4_q), .in4(register_5_q),
    .in5(register_6_q), .in6(register_7_q), .in7(register_8_q), .out(out_7), .sel(read_reg1[3:1]));  // open: en
  Multiplexer #(.select(3), .width(8)) multiplexer_2 (
    .in0(register_1_q), .in1(register_2_q), .in2(register_3_q), .in3(register_4_q), .in4(register_5_q),
    .in5(register_6_q), .in6(register_7_q), .in7(register_8_q), .out(out_8), .sel(read_reg2[3:1]));  // open: en
endmodule
