// Logisim project ALU.circ as structural Verilog
module ALU0 (
  input  [7:0] in_1,
  input  [7:0] in_2,
  output [7:0] ADD,
  output [7:0] SUB,
  output [7:0] AND,
  output [7:0] OR,
  output [7:0] NOR,
  output [7:0] SLL,
  output [7:0] out_9
);

  wire [2:0] bit_extender_1_out;
  wire [7:7] shifter_1_out, shifter_2_out;

  Bit_Extender #(.out_width(3)) bit_extender_1 (.in(in_2), .out(bit_extender_1_out));
  Adder adder_1 (.a(in_1), .b(in_2), .out(ADD), .cin(1'b0));  // open: cout
  Subtractor subtractor_1 (.a(in_1), .b(in_2), .out(SUB), .bin(1'b0));  // open: bout
  assign AND = in_1 & in_2;  // AND_Gate and_1, 8 bits wide
  assign OR = in_1 | in_2;  // OR_Gate or_1, 8 bits wide
  assign NOR = ~OR;  // NOT_Gate not_1, 8 bits wide
  Shifter shifter_1 (.in(in_1), .\dist (bit_extender_1_out), .out({shifter_1_out[7], SLL[6:0]}));
  Shifter #(.shift("lr")) shifter_2 (.in(in_1), .\dist (bit_extender_1_out), .out({shifter_2_out[7], out_9[6:0]}));

  assign out_9[7] = in_1[7];
  assign SLL[7] = in_1[7];

  // Notes on the sheet:
  //   SRL
endmodule

module ALU1 (
  input  in_1,
  input  [7:0] in_2,
  input  [7:0] in_3,
  input  [7:0] in_4,
  input  [2:0] in_5
);

  wire [7:0] alu0_1_add, alu0_1_and, alu0_1_nor, alu0_1_or, alu0_1_out_9, alu0_1_sll, alu0_1_sub,
       multiplexer_1_out, multiplexer_2_out;

  Multiplexer #(.width(8), .enable("false")) multiplexer_1 (
    .in0(in_3), .in1(in_4), .out(multiplexer_1_out), .sel(in_1));
  ALU0 alu0_1 (
    .in_1(in_2), .in_2(multiplexer_1_out), .ADD(alu0_1_add), .SUB(alu0_1_sub), .AND(alu0_1_and),
    .OR(alu0_1_or), .NOR(alu0_1_nor), .SLL(alu0_1_sll), .out_9(alu0_1_out_9));
  Multiplexer #(.select(3), .width(8), .enable("false")) multiplexer_2 (
    .in0(alu0_1_add), .in1(alu0_1_sub), .in2(alu0_1_and), .in3(alu0_1_or), .in4(alu0_1_nor),
    .in5(alu0_1_sll), .in6(alu0_1_out_9), .out(multiplexer_2_out), .sel(in_5));  // open: in7
endmodule
