// Logisim project MIPS.circ as structural Verilog
module BRANCH_offset (
  input  [19:0] in_1,
  output [7:0] out_2
);


  assign out_2 = in_1[7:0];
endmodule

module JUMP_address (
  input  [19:0] in_1,
  output [7:0] JUMP_address
);


  assign JUMP_address = in_1[15:8];
endmodule

module RAM (
  input  Reset,
  output [7:0] out_2,
  output [23:0] zero_t1,
  output [23:0] t2_t4,
  output [15:0] t5___sp
);

  wire Branch_control_selection_bit, clock_1_out, Control_unit_alusrc, Control_unit_beq, Control_unit_bne,
       Control_unit_jump, Control_unit_memread, Control_unit_memtoreg, Control_unit_memwrite,
       Control_unit_regdst, Control_unit_regwrite, mips_alu_8_bit_by_tushar_1_p4;
  wire [2:0] Control_unit_alu_control;
  wire [3:0] multiplexer_1_out;
  wire [7:0] adder_1_out, adder_2_out, Branch_offset_out_2, Jump_address_jump_address,
       mips_alu_8_bit_by_tushar_1_p5, multiplexer_2_out, multiplexer_3_out, multiplexer_4_out,
       Programme_counter_q, ram_1_data, Register_read_reg_1, Register_read_reg_2;
  wire [19:0] rom_1_data;

  Clock clock_1 (.out(clock_1_out));
  Register Programme_counter (
    .D(multiplexer_3_out), .en(1'b1), .Q(Programme_counter_q), .clk(clock_1_out), .clr(Reset));
  Adder adder_1 (.a(8'h1), .b(Programme_counter_q), .out(adder_1_out), .cin(1'b0));  // open: cout
  ROM #(.dataWidth(20)) rom_1 (.addr(Programme_counter_q), .data(rom_1_data), .sel(1'b1));
  Adder adder_2 (.a(adder_1_out), .b(Branch_offset_out_2), .out(adder_2_out), .cin(1'b0));  // open: cout
  BRANCH_offset Branch_offset (.out_2(Branch_offset_out_2), .in_1(rom_1_data));
  JUMP_address Jump_address (.in_1(rom_1_data), .JUMP_address(Jump_address_jump_address));
  control_unit Control_unit (
    .in_1(rom_1_data[19:16]), .Jump(Control_unit_jump), .RegDst(Control_unit_regdst),
    .ALUsrc(Control_unit_alusrc), .MemToReg(Control_unit_memtoreg), .RegWrite(Control_unit_regwrite),
    .MemRead(Control_unit_memread), .MemWrite(Control_unit_memwrite), .beq(Control_unit_beq),
    .bne(Control_unit_bne), .alu_control(Control_unit_alu_control));
  Multiplexer #(.width(4), .enable("false")) multiplexer_1 (
    .in0(rom_1_data[11:8]), .in1(rom_1_data[7:4]), .out(multiplexer_1_out), .sel(Control_unit_regdst));
  Multiplexer #(.width(8), .enable("false")) multiplexer_2 (
    .in0(adder_1_out), .in1(adder_2_out), .out(multiplexer_2_out), .sel(Branch_control_selection_bit));
  _8_bit_register Register (
    .read_reg1(rom_1_data[15:12]), .read_reg2(rom_1_data[11:8]), .write_reg(multiplexer_1_out),
    .write_date(out_2), .Reg_write(Control_unit_regwrite), .t5__sp(t5___sp), .Reset(Reset),
    .clock(clock_1_out), .Read_reg_1(Register_read_reg_1), .Read_reg_2(Register_read_reg_2),
    .zero___t1(zero_t1), .t2_t4(t2_t4));
  Multiplexer #(.width(8), .enable("false")) multiplexer_3 (
    .in0(multiplexer_2_out), .in1(Jump_address_jump_address), .out(multiplexer_3_out), .sel(Control_unit_jump));
  Multiplexer #(.width(8), .enable("false")) multiplexer_4 (
    .in0(Register_read_reg_2), .in1(rom_1_data[7:0]), .out(multiplexer_4_out), .sel(Control_unit_alusrc));
  // MIPS_ALU_8_bit_by_Tushar mips_alu_8_bit_by_tushar_1: pin names not known; wires that end beside it: Register_read_reg_1, multiplexer_4_out, Control_unit_alu_control, mips_alu_8_bit_by_tushar_1_p4, mips_alu_8_bit_by_tushar_1_p5
  BranchSelector Branch_control (
    .beq(Control_unit_beq), .bne(Control_unit_bne), .selection_bit(Branch_control_selection_bit),
    .alu_zero_input(mips_alu_8_bit_by_tushar_1_p4));
  RAM_part #(.bus("separate")) ram_1 (
    .addr(mips_alu_8_bit_by_tushar_1_p5), .din(Register_read_reg_2), .data(ram_1_data),
    .str(Control_unit_memwrite), .clk(clock_1_out), .ld(Control_unit_memread), .clr(Reset));  // open: sel
  Multiplexer #(.width(8), .enable("false")) multiplexer_5 (
    .in0(mips_alu_8_bit_by_tushar_1_p5), .in1(ram_1_data), .out(out_2), .sel(Control_unit_memtoreg));

  // Notes on the sheet:
  //   contents of rom_1 (hex, n*v repeats v):
  //   b07ff b0101 b0502 42102 62602 47600 17701 b7701 67400 230f7 a0c00 245f5 a0100
  //   Instruction memory
  //   Data memory
endmodule

module control_unit (
  input  [3:0] in_1,
  output Jump,
  output RegDst,
  output ALUsrc,
  output MemToReg,
  output RegWrite,
  output MemRead,
  output MemWrite,
  output beq,
  output bne,
  output [2:0] alu_control
);

  wire and_2_out, and_3_out, and_4_out, and_6_out, not_1_out, not_2_out, not_3_out, not_4_out, not_5_out,
       not_6_out, not_7_out, not_8_out, not_9_out, not_10_out, not_11_out, not_12_out, not_13_out,
       not_14_out, not_15_out;

  not not_1 (not_1_out, in_1[0]);
  not not_2 (not_2_out, in_1[2]);
  not not_3 (not_3_out, in_1[0]);
  not not_4 (not_4_out, in_1[3]);
  and and_1 (Jump, not_1_out, in_1[1], not_2_out, in_1[3]);
  and and_2 (and_2_out, in_1[0], in_1[2]);
  not not_5 (not_5_out, in_1[0]);
  not not_6 (not_6_out, in_1[1]);
  and and_3 (and_3_out, not_6_out, not_5_out, in_1[3]);
  and and_4 (and_4_out, in_1[0], in_1[1], not_7_out);
  not not_7 (not_7_out, in_1[3]);
  not not_8 (not_8_out, in_1[0]);
  not not_9 (not_9_out, in_1[3]);
  Multiplexer #(.select(4), .enable("false")) multiplexer_1 (
    .in0(1'b1), .in1(1'b1), .in2(1'b0), .in3(1'b0), .in4(1'b1), .in5(1'b0), .in6(1'b1), .in7(1'b0),
    .in8(1'b0), .in9(1'b0), .in10(1'b1), .in11(1'b1), .in12(1'b0), .in13(1'b0), .in14(1'b1), .in15(1'b0),
    .out(ALUsrc), .sel(in_1));
  and and_5 (MemToReg, not_3_out, in_1[1], not_4_out);
  Multiplexer #(.select(4), .enable("false")) multiplexer_2 (
    .in0(1'b1), .in1(1'b1), .in2(1'b0), .in3(1'b1), .in4(1'b0), .in5(1'b1), .in6(1'b1), .in7(1'b1),
    .in8(1'b1), .in9(1'b0), .in10(1'b0), .in11(1'b1), .in12(1'b1), .in13(1'b1), .in14(1'b1), .in15(1'b1),
    .out(RegWrite), .sel(in_1));
  and and_6 (and_6_out, not_8_out, in_1[2], not_9_out);
  not not_10 (not_10_out, in_1[1]);
  not not_11 (not_11_out, in_1[0]);
  not not_12 (not_12_out, in_1[2]);
  not not_13 (not_13_out, in_1[3]);
  not not_14 (not_14_out, in_1[1]);
  not not_15 (not_15_out, in_1[2]);
  alu_control u_ALU_control (.abcd(in_1), .out_2(alu_control));
  or or_1 (RegDst, and_2_out, and_3_out, and_4_out);
  and and_7 (MemRead, and_6_out, in_1[1]);
  and and_8 (MemWrite, and_6_out, not_10_out);
  and and_9 (beq, not_11_out, in_1[1], not_12_out, not_13_out);
  and and_10 (bne, in_1[0], not_14_out, not_15_out, in_1[3]);
endmodule

module alu_control (
  input  [3:0] abcd,
  output [2:0] out_2
);

  wire and_1_out, and_2_out, and_3_out, and_4_out, and_5_out, and_6_out, and_7_out, and_8_out, and_9_out,
       and_10_out, not_1_out, not_2_out, not_3_out, not_4_out, or_1_out, or_2_out;

  not not_1 (not_1_out, abcd[3]);
  not not_2 (not_2_out, abcd[0]);
  not not_3 (not_3_out, abcd[2]);
  not not_4 (not_4_out, abcd[1]);
  and and_1 (and_1_out, not_1_out, abcd[2], not_2_out);
  and and_2 (and_2_out, abcd[3], abcd[1], abcd[0]);
  and and_3 (and_3_out, abcd[3], not_4_out, abcd[0]);
  and and_4 (and_4_out, not_3_out, not_4_out, abcd[0]);
  and and_5 (and_5_out, not_1_out, not_3_out, abcd[1], not_2_out);
  and and_6 (and_6_out, abcd[3], abcd[2], not_2_out);
  and and_7 (and_7_out, not_3_out, not_4_out, not_2_out);
  and and_8 (and_8_out, not_1_out, not_3_out, abcd[1], abcd[0]);
  and and_9 (and_9_out, not_1_out, abcd[2], not_4_out, abcd[0]);
  and and_10 (and_10_out, not_1_out, abcd[2], abcd[1], abcd[0]);
  or or_1 (or_1_out, and_1_out, and_2_out);
  or or_2 (or_2_out, and_3_out, and_4_out, and_5_out);
  Priority_Encoder priority_encoder_1 (
    .in0(or_1_out), .in1(or_2_out), .in2(and_6_out), .in3(and_7_out), .in4(and_8_out), .in5(and_9_out),
    .in6(and_10_out), .out(out_2));  // open: in7, en_in, gs, en_out

  // Notes on the sheet:
  //   a_not
  //   d_not
  //   c_not
  //   b_not
  //   d
endmodule

module _8_bit_register (
  input  Reg_write,
  input  [3:0] read_reg1,
  input  [3:0] read_reg2,
  input  [3:0] write_reg,
  input  [7:0] write_date,
  input  clock,
  input  Reset,
  output [15:0] t5__sp,
  output [7:0] Read_reg_1,
  output [7:0] Read_reg_2,
  output [23:0] zero___t1,
  output [23:0] t2_t4
);

  wire and_1_out, and_2_out, and_3_out, and_4_out, and_5_out, and_6_out, and_7_out, and_8_out,
       decoder_1_out0, decoder_1_out1, decoder_1_out2, decoder_1_out3, decoder_1_out4, decoder_1_out5,
       decoder_1_out6, decoder_1_out7;

  Decoder #(.select(3), .enable("false")) decoder_1 (
    .out0(decoder_1_out0), .out1(decoder_1_out1), .out2(decoder_1_out2), .out3(decoder_1_out3),
    .out4(decoder_1_out4), .out5(decoder_1_out5), .out6(decoder_1_out6), .out7(decoder_1_out7),
    .sel(write_reg[2:0]));
  and and_1 (and_1_out, decoder_1_out0, Reg_write);
  and and_2 (and_2_out, decoder_1_out1, Reg_write);
  and and_3 (and_3_out, decoder_1_out2, Reg_write);
  and and_4 (and_4_out, decoder_1_out3, Reg_write);
  and and_5 (and_5_out, decoder_1_out4, Reg_write);
  and and_6 (and_6_out, decoder_1_out5, Reg_write);
  and and_7 (and_7_out, decoder_1_out6, Reg_write);
  and and_8 (and_8_out, decoder_1_out7, Reg_write);
  Register register_1 (.D({8{1'b0}}), .Q(zero___t1[23:16]), .clk(clock), .clr(and_1_out));  // open: en
  Register register_2 (.D(write_date), .en(and_2_out), .Q(zero___t1[15:8]), .clk(clock), .clr(Reset));
  Register register_3 (.D(write_date), .en(and_3_out), .Q(zero___t1[7:0]), .clk(clock), .clr(Reset));
  Register register_4 (.D(write_date), .en(and_4_out), .Q(t2_t4[23:16]), .clk(clock), .clr(Reset));
  Register register_5 (.D(write_date), .en(and_5_out), .Q(t2_t4[15:8]), .clk(clock), .clr(Reset));
  Register register_6 (.D(write_date), .en(and_6_out), .Q(t2_t4[7:0]), .clk(clock), .clr(Reset));
  Register register_7 (.D(write_date), .en(and_7_out), .Q(t5__sp[15:8]), .clk(clock), .clr(Reset));
  Register SP (.D(write_date), .en(and_8_out), .Q(t5__sp[7:0]), .clk(clock));  // open: clr
  Multiplexer #(.select(3), .width(8), .enable("false")) multiplexer_1 (
    .in0(zero___t1[23:16]), .in1(zero___t1[15:8]), .in2(zero___t1[7:0]), .in3(t2_t4[23:16]),
    .in4(t2_t4[15:8]), .in5(t2_t4[7:0]), .in6(t5__sp[15:8]), .in7(t5__sp[7:0]), .out(Read_reg_1),
    .sel(read_reg1[2:0]));
  Multiplexer #(.select(3), .width(8), .enable("false")) multiplexer_2 (
    .in0(zero___t1[23:16]), .in1(zero___t1[15:8]), .in2(zero___t1[7:0]), .in3(t2_t4[23:16]),
    .in4(t2_t4[15:8]), .in5(t2_t4[7:0]), .in6(t5__sp[15:8]), .in7(t5__sp[7:0]), .out(Read_reg_2),
    .sel(read_reg2[2:0]));
endmodule

module BranchSelector (
  input  beq,
  input  bne,
  input  alu_zero_input,
  output selection_bit
);

  wire and_1_out, and_2_out, not_1_out;

  not not_1 (not_1_out, alu_zero_input);
  and and_1 (and_1_out, beq, alu_zero_input);
  and and_2 (and_2_out, bne, not_1_out);
  or or_1 (selection_bit, and_1_out, and_2_out);
endmodule
