// Logisim project alu_control.circ as structural Verilog: 1 circuit, main circuit main
module main (
  input  [3:0] abcd,
  output [2:0] out_2
);

  wire and_1_out, and_2_out, and_3_out, and_4_out, and_5_out, and_6_out, and_7_out, and_8_out, and_9_out,
       and_10_out, not_1_out, not_2_out, not_3_out, not_4_out, or_1_out, or_2_out;

  not not_1 (not_1_out, abcd[3]);
  not not_2 (not_2_out, abcd[1]);
  not not_3 (not_3_out, abcd[0]);
  not not_4 (not_4_out, abcd[2]);
  and and_1 (and_1_out, not_1_out, abcd[2], not_3_out);
  and and_2 (and_2_out, abcd[3], abcd[1], abcd[0]);
  and and_3 (and_3_out, abcd[3], not_2_out, abcd[0]);
  and and_4 (and_4_out, not_4_out, not_2_out, abcd[0]);
  and and_5 (and_5_out, not_1_out, not_4_out, abcd[1], not_3_out);
  and and_6 (and_6_out, abcd[3], abcd[2], not_3_out);
  and and_7 (and_7_out, not_4_out, not_2_out, not_3_out);
  and and_8 (and_8_out, not_1_out, not_4_out, abcd[1], abcd[0]);
  and and_9 (and_9_out, not_1_out, abcd[2], not_2_out, abcd[0]);
  and and_10 (and_10_out, not_1_out, abcd[2], abcd[1], abcd[0]);
  or or_1 (or_1_out, and_1_out, and_2_out);
  or or_2 (or_2_out, and_3_out, and_4_out, and_5_out);
  Priority_Encoder priority_encoder_1 (
    .in0(or_1_out), .in1(or_2_out), .in2(and_6_out), .in3(and_7_out), .in4(and_8_out), .in5(and_9_out),
    .in6(and_10_out), .out(out_2));  // open: in7, en_in, gs, en_out

  // Notes on the sheet:
  //   a_not
  //   d_not
  //   c_not
  //   b_not
  //   d
endmodule
