// Logisim project control_unit.circ as structural Verilog: 1 circuit, main circuit main
module main (
  input  [3:0] in_1,
  output Jump,
  output RegDst,
  output ALUsrc,
  output MemToReg,
  output RegWrite,
  output MemRead,
  output MemWrite,
  output beq,
  output bne
);

  wire and_2_out, and_3_out, and_4_out, and_6_out, not_1_out, not_2_out, not_3_out, not_4_out, not_5_out,
       not_6_out, not_7_out, not_8_out, not_9_out, not_10_out, not_11_out, not_12_out, not_13_out,
       not_14_out, not_15_out;

  not not_1 (not_1_out, in_1[0]);
  not not_2 (not_2_out, in_1[2]);
  not not_3 (not_3_out, in_1[0]);
  not not_4 (not_4_out, in_1[3]);
  and and_1 (Jump, not_1_out, in_1[1], not_2_out, in_1[3]);
  and and_2 (and_2_out, in_1[0], in_1[2]);
  not not_5 (not_5_out, in_1[0]);
  not not_6 (not_6_out, in_1[1]);
  and and_3 (and_3_out, not_6_out, not_5_out, in_1[3]);
  and and_4 (and_4_out, in_1[0], in_1[1], not_7_out);
  not not_7 (not_7_out, in_1[3]);
  not not_8 (not_8_out, in_1[0]);
  not not_9 (not_9_out, in_1[3]);
  Multiplexer #(.select(4), .enable("false")) multiplexer_1 (
    .in0(1'b1), .in1(1'b1), .in2(1'b0), .in3(1'b0), .in4(1'b1), .in5(1'b0), .in6(1'b1), .in7(1'b0),
    .in8(1'b0), .in9(1'b0), .in10(1'b1), .in11(1'b1), .in12(1'b0), .in13(1'b0), .in14(1'b1), .in15(1'b0),
    .out(ALUsrc), .sel(in_1));
  and and_5 (MemToReg, not_3_out, in_1[1], not_4_out);
  Multiplexer #(.select(4), .enable("false")) multiplexer_2 (
    .in0(1'b1), .in1(1'b1), .in2(1'b0), .in3(1'b1), .in4(1'b0), .in5(1'b1), .in6(1'b1), .in7(1'b1),
    .in8(1'b1), .in9(1'b0), .in10(1'b0), .in11(1'b1), .in12(1'b1), .in13(1'b1), .in14(1'b1), .in15(1'b1),
    .out(RegWrite), .sel(in_1));
  and and_6 (and_6_out, not_8_out, in_1[2], not_9_out);
  not not_10 (not_10_out, in_1[1]);
  not not_11 (not_11_out, in_1[0]);
  not not_12 (not_12_out, in_1[2]);
  not not_13 (not_13_out, in_1[3]);
  not not_14 (not_14_out, in_1[1]);
  not not_15 (not_15_out, in_1[2]);
  or or_1 (RegDst, and_2_out, and_3_out, and_4_out);
  and and_7 (MemRead, and_6_out, in_1[1]);
  and and_8 (MemWrite, and_6_out, not_10_out);
  and and_9 (beq, not_11_out, in_1[1], not_12_out, not_13_out);
  and and_10 (bne, in_1[0], not_14_out, not_15_out, in_1[3]);
endmodule
