// Logisim project instruction_memory.circ as structural Verilog: 3 circuits, main circuit main
module main (
  input  normal_or_branch,
  input  in_2,
  output [19:0] _20_bit_instruction
);

  wire clock_1_out, Jump_address_is_not_jump_instruction;
  wire [7:0] adder_1_out, adder_2_out, Branch_offset_out_2, Jump_address_jump_address, multiplexer_1_out,
       multiplexer_2_out, Programme_counter_q;

  Clock clock_1 (.out(clock_1_out));
  Register Programme_counter (.D(multiplexer_2_out), .en(1'b1), .Q(Programme_counter_q), .clk(clock_1_out), .clr(in_2));
  Adder adder_1 (.a(8'h1), .b(Programme_counter_q), .out(adder_1_out), .cin(1'b0));  // open: cout
  ROM #(.dataWidth(20)) rom_1 (.addr(Programme_counter_q), .data(_20_bit_instruction), .sel(1'b1));
  Adder adder_2 (.a(adder_1_out), .b(Branch_offset_out_2), .out(adder_2_out), .cin(1'b0));  // open: cout
  BRANCH_offset Branch_offset (.out_2(Branch_offset_out_2), .in_1(_20_bit_instruction));
  JUMP_address Jump_address (
    .in_1(_20_bit_instruction), .JUMP_address(Jump_address_jump_address),
    .is_not_jump_instruction(Jump_address_is_not_jump_instruction));
  Multiplexer #(.width(8), .enable("false")) multiplexer_1 (
    .in0(adder_1_out), .in1(adder_2_out), .out(multiplexer_1_out), .sel(normal_or_branch));
  Multiplexer #(.width(8), .enable("false")) multiplexer_2 (
    .in0(Jump_address_jump_address), .in1(multiplexer_1_out), .out(multiplexer_2_out),
    .sel(Jump_address_is_not_jump_instruction));

  // Notes on the sheet:
  //   contents of rom_1 (hex, n*v repeats v):
  //   f2010 21207 21206 b320a d3420 1320a 84530 5205 c4530 e5205 a0e00 34530 42118 64320 213fa 913f9 a0000
  //   84530 5205
  //   Instruction memory
  //   jump or normal/branch
endmodule

module JUMP_address (
  input  [19:0] in_1,
  output [7:0] JUMP_address,
  output is_not_jump_instruction
);

  wire not_1_out, not_2_out;

  not not_1 (not_1_out, in_1[16]);
  not not_2 (not_2_out, in_1[18]);
  nand nand_1 (is_not_jump_instruction, not_1_out, in_1[17], not_2_out, in_1[19]);

  assign JUMP_address = in_1[15:8];
endmodule

module BRANCH_offset (
  input  [19:0] in_1,
  output [7:0] out_2
);


  assign out_2 = in_1[7:0];
endmodule
