// Logisim project Pipeline.circ as structural Verilog
module control_unit (
  input  [3:0] in_1,
  output Jump,
  output RegDst,
  output ALUsrc,
  output MemToReg,
  output RegWrite,
  output MemRead,
  output MemWrite,
  output beq,
  output bne,
  output [2:0] alu_control
);

  wire and_2_out, and_3_out, and_4_out, and_6_out, not_1_out, not_2_out, not_3_out, not_4_out, not_5_out,
       not_6_out, not_7_out, not_8_out, not_9_out, not_10_out, not_11_out, not_12_out, not_13_out,
       not_14_out, not_15_out;

  not not_1 (not_1_out, in_1[0]);
  not not_2 (not_2_out, in_1[2]);
  not not_3 (not_3_out, in_1[0]);
  not not_4 (not_4_out, in_1[3]);
  and and_1 (Jump, not_1_out, in_1[1], not_2_out, in_1[3]);
  and and_2 (and_2_out, in_1[0], in_1[2]);
  not not_5 (not_5_out, in_1[0]);
  not not_6 (not_6_out, in_1[1]);
  and and_3 (and_3_out, not_6_out, not_5_out, in_1[3]);
  and and_4 (and_4_out, in_1[0], in_1[1], not_7_out);
  not not_7 (not_7_out, in_1[3]);
  not not_8 (not_8_out, in_1[0]);
  not not_9 (not_9_out, in_1[3]);
  Multiplexer #(.select(4), .enable("false")) multiplexer_1 (
    .in0(1'b1), .in1(1'b1), .in2(1'b0), .in3(1'b0), .in4(1'b1), .in5(1'b0), .in6(1'b1), .in7(1'b0),
    .in8(1'b0), .in9(1'b0), .in10(1'b1), .in11(1'b1), .in12(1'b0), .in13(1'b0), .in14(1'b1), .in15(1'b0),
    .out(ALUsrc), .sel(in_1));
  and and_5 (MemToReg, not_3_out, in_1[1], not_4_out);
  Multiplexer #(.select(4), .enable("false")) multiplexer_2 (
    .in0(1'b1), .in1(1'b1), .in2(1'b0), .in3(1'b1), .in4(1'b0), .in5(1'b1), .in6(1'b1), .in7(1'b1),
    .in8(1'b1), .in9(1'b0), .in10(1'b0), .in11(1'b1), .in12(1'b1), .in13(1'b1), .in14(1'b1), .in15(1'b1),
    .out(RegWrite), .sel(in_1));
  and and_6 (and_6_out, not_8_out, in_1[2], not_9_out);
  not not_10 (not_10_out, in_1[1]);
  not not_11 (not_11_out, in_1[0]);
  not not_12 (not_12_out, in_1[2]);
  not not_13 (not_13_out, in_1[3]);
  not not_14 (not_14_out, in_1[1]);
  not not_15 (not_15_out, in_1[2]);
  alu_control u_ALU_control (.abcd(in_1), .out_2(alu_control));
  or or_1 (RegDst, and_2_out, and_3_out, and_4_out);
  and and_7 (MemRead, and_6_out, in_1[1]);
  and and_8 (MemWrite, and_6_out, not_10_out);
  and and_9 (beq, not_11_out, in_1[1], not_12_out, not_13_out);
  and and_10 (bne, in_1[0], not_14_out, not_15_out, in_1[3]);
endmodule

module alu_control (
  input  [3:0] abcd,
  output [2:0] out_2
);

  wire and_1_out, and_2_out, and_3_out, and_4_out, and_5_out, and_6_out, and_7_out, and_8_out, and_9_out,
       and_10_out, not_1_out, not_2_out, not_3_out, not_4_out, or_1_out, or_2_out;

  not not_1 (not_1_out, abcd[3]);
  not not_2 (not_2_out, abcd[1]);
  not not_3 (not_3_out, abcd[0]);
  not not_4 (not_4_out, abcd[2]);
  and and_1 (and_1_out, not_1_out, abcd[2], not_3_out);
  and and_2 (and_2_out, abcd[3], abcd[1], abcd[0]);
  and and_3 (and_3_out, abcd[3], not_2_out, abcd[0]);
  and and_4 (and_4_out, not_4_out, not_2_out, abcd[0]);
  and and_5 (and_5_out, not_1_out, not_4_out, abcd[1], not_3_out);
  and and_6 (and_6_out, abcd[3], abcd[2], not_3_out);
  and and_7 (and_7_out, not_4_out, not_2_out, not_3_out);
  and and_8 (and_8_out, not_1_out, not_4_out, abcd[1], abcd[0]);
  and and_9 (and_9_out, not_1_out, abcd[2], not_2_out, abcd[0]);
  and and_10 (and_10_out, not_1_out, abcd[2], abcd[1], abcd[0]);
  or or_1 (or_1_out, and_1_out, and_2_out);
  or or_2 (or_2_out, and_3_out, and_4_out, and_5_out);
  Priority_Encoder priority_encoder_1 (
    .in0(or_1_out), .in1(or_2_out), .in2(and_6_out), .in3(and_7_out), .in4(and_8_out), .in5(and_9_out),
    .in6(and_10_out), .out(out_2));  // open: in7, en_in, gs, en_out

  // Notes on the sheet:
  //   a_not
  //   d_not
  //   c_not
  //   b_not
  //   d
endmodule

module _8_bit_register (
  input  Reg_write,
  input  [3:0] read_reg1,
  input  [3:0] read_reg2,
  input  [3:0] write_reg,
  input  [7:0] write_data,
  input  clock,
  input  Reset,
  output [15:0] t5__sp,
  output [7:0] Read_reg_1,
  output [7:0] Read_reg_2,
  output [23:0] zero___t1,
  output [23:0] t2_t4
);

  wire and_1_out, and_2_out, and_3_out, and_4_out, and_5_out, and_6_out, and_7_out, and_8_out,
       decoder_1_out0, decoder_1_out1, decoder_1_out2, decoder_1_out3, decoder_1_out4, decoder_1_out5,
       decoder_1_out6, decoder_1_out7;

  Decoder #(.select(3), .enable("false")) decoder_1 (
    .out0(decoder_1_out0), .out1(decoder_1_out1), .out2(decoder_1_out2), .out3(decoder_1_out3),
    .out4(decoder_1_out4), .out5(decoder_1_out5), .out6(decoder_1_out6), .out7(decoder_1_out7),
    .sel(write_reg[2:0]));
  and and_1 (and_1_out, decoder_1_out0, Reg_write);
  and and_2 (and_2_out, decoder_1_out1, Reg_write);
  and and_3 (and_3_out, decoder_1_out2, Reg_write);
  and and_4 (and_4_out, decoder_1_out3, Reg_write);
  and and_5 (and_5_out, decoder_1_out4, Reg_write);
  and and_6 (and_6_out, decoder_1_out5, Reg_write);
  and and_7 (and_7_out, decoder_1_out6, Reg_write);
  and and_8 (and_8_out, decoder_1_out7, Reg_write);
  Register register_1 (.D({8{1'b0}}), .en(and_1_out), .Q(zero___t1[23:16]), .clk(clock), .clr(Reset));
  Register register_2 (.D(write_data), .en(and_2_out), .Q(zero___t1[15:8]), .clk(clock), .clr(Reset));
  Register register_3 (.D(write_data), .en(and_3_out), .Q(zero___t1[7:0]), .clk(clock), .clr(Reset));
  Register register_4 (.D(write_data), .en(and_4_out), .Q(t2_t4[23:16]), .clk(clock), .clr(Reset));
  Register register_5 (.D(write_data), .en(and_5_out), .Q(t2_t4[15:8]), .clk(clock), .clr(Reset));
  Register register_6 (.D(write_data), .en(and_6_out), .Q(t2_t4[7:0]), .clk(clock), .clr(Reset));
  Register register_7 (.D(write_data), .en(and_7_out), .Q(t5__sp[15:8]), .clk(clock), .clr(Reset));
  Register SP (.D(write_data), .en(and_8_out), .Q(t5__sp[7:0]), .clk(clock));  // open: clr
  Multiplexer #(.select(3), .width(8), .enable("false")) multiplexer_1 (
    .in0(zero___t1[23:16]), .in1(zero___t1[15:8]), .in2(zero___t1[7:0]), .in3(t2_t4[23:16]),
    .in4(t2_t4[15:8]), .in5(t2_t4[7:0]), .in6(t5__sp[15:8]), .in7(t5__sp[7:0]), .out(Read_reg_1),
    .sel(read_reg1[2:0]));
  Multiplexer #(.select(3), .width(8), .enable("false")) multiplexer_2 (
    .in0(zero___t1[23:16]), .in1(zero___t1[15:8]), .in2(zero___t1[7:0]), .in3(t2_t4[23:16]),
    .in4(t2_t4[15:8]), .in5(t2_t4[7:0]), .in6(t5__sp[15:8]), .in7(t5__sp[7:0]), .out(Read_reg_2),
    .sel(read_reg2[2:0]));
endmodule

module pipelined_MIPS (
  input  reset,
  input  [7:0] REgInitData,
  input  [3:0] RegInitAddress,
  input  RegInitSelect,
  output [23:0] zero_t1,
  output [23:0] t2_t4,
  output [15:0] t5___sp
);

  wire and_1_out, and_2_out, Control_unit_regwrite, Normal_Execution_Clock_out, or_1_out, RegInitClock_out;
  wire [1:0] forwarda_unit_1_out_4, forwardb_uint_1_out_4;
  wire [2:0] Control_unit_alu_control, id_ex_1_alu_cntrl_2;
  wire [3:0] ex_mem_1_rd_2, id_ex_1_rd_2, id_ex_1_rs_2, id_ex_1_rt_2, mem_wb_1_rd_2, multiplexer_2_out;
  wire [7:0] adder_1_out, ex_mem_1_alu_result_2, id_ex_1_read1_2, id_ex_1_read2_2, mem_wb_1_alu_result_2,
       mips_alu_8_bit_by_tushar_1_p4, multiplexer_1_out, multiplexer_3_out, multiplexer_4_out,
       Programme_counter_q, Register_read_reg_1, Register_read_reg_2;
  wire [19:0] IF_ID_q, rom_1_data;

  Clock Normal_Execution_Clock (.out(Normal_Execution_Clock_out));
  and and_1 (and_1_out, Normal_Execution_Clock_out, ~RegInitSelect);  // AND_Gate
  Register Programme_counter (.D(adder_1_out), .en(1'b1), .Q(Programme_counter_q), .clk(and_1_out), .clr(reset));
  Clock RegInitClock (.out(RegInitClock_out));
  Adder adder_1 (.a(8'h1), .b(Programme_counter_q), .out(adder_1_out), .cin(1'b0));  // open: cout
  ROM #(.dataWidth(20)) rom_1 (.addr(Programme_counter_q), .data(rom_1_data), .sel(1'b1));
  Register #(.width(20)) IF_ID (.D(rom_1_data), .en(1'b1), .Q(IF_ID_q), .clk(and_1_out), .clr(reset));
  Multiplexer #(.width(8), .enable("false")) multiplexer_1 (
    .in0(mem_wb_1_alu_result_2), .in1(REgInitData), .out(multiplexer_1_out), .sel(RegInitSelect));
  and and_2 (and_2_out, RegInitSelect, RegInitClock_out);
  Multiplexer #(.width(4), .enable("false")) multiplexer_2 (
    .in0(mem_wb_1_rd_2), .in1(RegInitAddress), .out(multiplexer_2_out), .sel(RegInitSelect));
  control_unit Control_unit (
    .in_1(IF_ID_q[19:16]), .RegWrite(Control_unit_regwrite), .alu_control(Control_unit_alu_control));  // open: Jump, RegDst, ALUsrc, MemToReg, MemRead, MemWrite, beq, bne
  _8_bit_register Register (
    .read_reg1(IF_ID_q[15:12]), .read_reg2(IF_ID_q[11:8]), .write_reg(multiplexer_2_out),
    .write_data(multiplexer_1_out), .Reg_write(Control_unit_regwrite), .t5__sp(t5___sp), .Reset(reset),
    .clock(or_1_out), .Read_reg_1(Register_read_reg_1), .Read_reg_2(Register_read_reg_2),
    .zero___t1(zero_t1), .t2_t4(t2_t4));
  or or_1 (or_1_out, and_1_out, and_2_out);
  ID_EX id_ex_1 (
    .read1(Register_read_reg_1), .read2(Register_read_reg_2), .rs(IF_ID_q[15:12]), .rt(IF_ID_q[11:8]),
    .rd(IF_ID_q[7:4]), .alu_cntrl(Control_unit_alu_control), .clock(and_1_out), .reset(reset),
    .read1_2(id_ex_1_read1_2), .read2_2(id_ex_1_read2_2), .rs_2(id_ex_1_rs_2), .rt_2(id_ex_1_rt_2),
    .rd_2(id_ex_1_rd_2), .alu_cntrl_2(id_ex_1_alu_cntrl_2));
  forwardA_unit forwarda_unit_1 (
    .ID_EX_rs(id_ex_1_rs_2), .EX_MEM_rd(ex_mem_1_rd_2), .in_3(mem_wb_1_rd_2), .out_4(forwarda_unit_1_out_4));
  Multiplexer #(.select(2), .width(8), .enable("false")) multiplexer_3 (
    .in0(id_ex_1_read1_2), .in1(mem_wb_1_alu_result_2), .in2(ex_mem_1_alu_result_2), .out(multiplexer_3_out),
    .sel(forwarda_unit_1_out_4));  // open: in3
  Multiplexer #(.select(2), .width(8), .disabled(0), .enable("false")) multiplexer_4 (
    .in0(id_ex_1_read2_2), .in1(mem_wb_1_alu_result_2), .in2(ex_mem_1_alu_result_2), .out(multiplexer_4_out),
    .sel(forwardb_uint_1_out_4));  // open: in3
  forwardB_uint forwardb_uint_1 (
    .ID_EX_rt(id_ex_1_rt_2), .EX_MEM_rd(ex_mem_1_rd_2), .in_3(mem_wb_1_rd_2), .out_4(forwardb_uint_1_out_4));
  // MIPS_ALU_8_bit_by_Tushar mips_alu_8_bit_by_tushar_1: pin names not known; wires that end beside it: multiplexer_3_out, multiplexer_4_out, id_ex_1_alu_cntrl_2, mips_alu_8_bit_by_tushar_1_p4
  EX_MEM ex_mem_1 (
    .alu_result(mips_alu_8_bit_by_tushar_1_p4), .rd(id_ex_1_rd_2), .clock(and_1_out), .reset(reset),
    .alu_result_2(ex_mem_1_alu_result_2), .rd_2(ex_mem_1_rd_2));
  RAM #(.bus("separate")) ram_1 (.addr({8{1'b0}}), .clk(and_1_out));  // open: din, data, str, sel, ld, clr
  MEM_WB mem_wb_1 (
    .alu_result(ex_mem_1_alu_result_2), .rd(ex_mem_1_rd_2), .clock(and_1_out), .reset(reset),
    .alu_result_2(mem_wb_1_alu_result_2), .rd_2(mem_wb_1_rd_2));

  // Notes on the sheet:
  //   Instruction memory
  //   contents of rom_1 (hex, n*v repeats v):
  //   f1120 f1330 f3440 f3540 f4210
  //   Data memory
endmodule

module ID_EX (
  input  [7:0] read1,
  input  [7:0] read2,
  input  [3:0] rs,
  input  [3:0] rt,
  input  [3:0] rd,
  input  [2:0] alu_cntrl,
  input  clock,
  input  reset,
  output [7:0] read1_2,
  output [7:0] read2_2,
  output [3:0] rs_2,
  output [3:0] rt_2,
  output [3:0] rd_2,
  output [2:0] alu_cntrl_2
);

  Register register_1 (.D(read1), .en(1'b1), .Q(read1_2), .clk(clock), .clr(reset));
  Register register_2 (.D(read2), .en(1'b1), .Q(read2_2), .clk(clock), .clr(reset));
  Register #(.width(4)) register_3 (.D(rs), .en(1'b1), .Q(rs_2), .clk(clock), .clr(reset));
  Register #(.width(4)) register_4 (.D(rt), .en(1'b1), .Q(rt_2), .clk(clock), .clr(reset));
  Register #(.width(4)) register_5 (.D(rd), .en(1'b1), .Q(rd_2), .clk(clock), .clr(reset));
  Register #(.width(3)) register_6 (.D(alu_cntrl), .en(1'b1), .Q(alu_cntrl_2), .clk(clock), .clr(reset));

  // Notes on the sheet:
  //   read1
  //   rs
  //   rt
  //   rd
  //   alu_ control
endmodule

module EX_MEM (
  input  [7:0] alu_result,
  input  [3:0] rd,
  input  clock,
  input  reset,
  output [7:0] alu_result_2,
  output [3:0] rd_2
);

  Register register_1 (.D(alu_result), .en(1'b1), .Q(alu_result_2), .clk(clock), .clr(reset));
  Register #(.width(4)) register_2 (.D(rd), .en(1'b1), .Q(rd_2), .clk(clock), .clr(reset));
endmodule

module MEM_WB (
  input  [7:0] alu_result,
  input  [3:0] rd,
  input  clock,
  input  reset,
  output [7:0] alu_result_2,
  output [3:0] rd_2
);

  Register register_1 (.D(alu_result), .en(1'b1), .Q(alu_result_2), .clk(clock), .clr(reset));
  Register #(.width(4)) register_2 (.D(rd), .en(1'b1), .Q(rd_2), .clk(clock), .clr(reset));
endmodule

module forwardB_uint (
  input  [3:0] ID_EX_rt,
  input  [3:0] EX_MEM_rd,
  input  [3:0] in_3,
  output [1:0] out_4
);

  wire [1:0] comparator_1_eq;

  Comparator #(.width(4)) comparator_1 (.a(ID_EX_rt), .b(EX_MEM_rd), .eq(comparator_1_eq[0]));  // open: gt, lt
  Comparator #(.width(4)) comparator_2 (.a(ID_EX_rt), .b(in_3), .eq(comparator_1_eq[1]));  // open: gt, lt
  Multiplexer #(.select(2), .width(2), .enable("false")) multiplexer_1 (
    .in0(2'b00), .in1(2'b10), .in2(2'b01), .in3(2'b10), .out(out_4), .sel(comparator_1_eq));

  // Notes on the sheet:
  //   MEM_WB_rd
  //   data_hazard
  //   memory_hazard
endmodule

module forwardA_unit (
  input  [3:0] ID_EX_rs,
  input  [3:0] EX_MEM_rd,
  input  [3:0] in_3,
  output [1:0] out_4
);

  wire [1:0] comparator_1_eq;

  Comparator #(.width(4)) comparator_1 (.a(ID_EX_rs), .b(EX_MEM_rd), .eq(comparator_1_eq[0]));  // open: gt, lt
  Comparator #(.width(4)) comparator_2 (.a(ID_EX_rs), .b(in_3), .eq(comparator_1_eq[1]));  // open: gt, lt
  Multiplexer #(.select(2), .width(2), .enable("false")) multiplexer_1 (
    .in0(2'b00), .in1(2'b10), .in2(2'b01), .in3(2'b10), .out(out_4), .sel(comparator_1_eq));

  // Notes on the sheet:
  //   MEM_WB_rd
  //   data_hazard
  //   memory_hazard
endmodule
