// Logisim project fp_adder_circuit_final3.circ as structural Verilog: 10 circuits, main circuit main
module main (
  input  [15:0] in_1,
  input  [15:0] in_2,
  output [15:0] out_3,
  output overflow,
  output underflow
);

  FP_adder fp_adder_1 (.in_1(in_1), .in_2(in_2), .Answer(out_3), .Overflow(overflow), .Underflow(underflow));

  // Notes on the sheet:
  //   result
endmodule

// SIgnificand Builder
module Significand_Builder (
  input  [10:0] in_1,
  input  in_2,
  output [16:0] out_3
);


  assign out_3 = {in_2, 3'b001, in_1, 2'b00};
endmodule

module Right_Shifter (
  input  [16:0] in_1,
  input  [3:0] in_2,
  input  in_3,
  output [16:0] out_4
);

  wire [3:0] adder_1_out, multiplexer_1_out, not_1_out;

  assign not_1_out = ~in_2;  // NOT_Gate not_1, 4 bits wide
  Adder #(.width(4)) adder_1 (.a(not_1_out), .b(4'b0000), .out(adder_1_out), .cin(1'b1));  // open: cout
  Multiplexer #(.width(4), .enable("false")) multiplexer_1 (
    .in0(in_2), .in1(adder_1_out), .out(multiplexer_1_out), .sel(in_3));
  Shifter #(.width(16), .shift("lr")) shifter_1 (.in(in_1[15:0]), .\dist (multiplexer_1_out), .out(out_4[15:0]));

  assign out_4[16] = in_1[16];

  // Notes on the sheet:
  //   Sign bit( No need to shift )
endmodule

module Adder_preprocessor (
  input  [16:0] in_1,
  output [15:0] out_2
);

  wire [15:0] adder_1_out, not_1_out;

  assign not_1_out = ~in_1[15:0];  // NOT_Gate not_1, 16 bits wide
  Adder #(.width(16)) adder_1 (.a(not_1_out), .b({16{1'b0}}), .out(adder_1_out), .cin(1'b1));  // open: cout
  Multiplexer #(.width(16), .enable("false")) multiplexer_1 (
    .in0(in_1[15:0]), .in1(adder_1_out), .out(out_2), .sel(in_1[16]));
endmodule

module FP_adder (
  input  [15:0] in_1,
  input  [15:0] in_2,
  output [15:0] Answer,
  output Overflow,
  output Underflow
);

  wire normalize_sum_1_out_5, normalize_sum_2_out_5, Overflow_Underflow_Handler_overflow,
       Overflow_Underflow_Handler_underflow, subtractor_1_bout, Zero_Handler_out_4;
  wire [3:0] multiplexer_1_out, normalize_sum_1_exponent, normalize_sum_2_exponent, subtractor_1_out;
  wire [15:0] adder_1_out, adder_2_out, Adder_preprocessor_2_out_2, Adder_preprocessor_out_2,
       multiplexer_4_out, normalize_sum_1_out_3, normalize_sum_2_out_3, not_1_out,
       Overflow_Underflow_Handler_out_6, rounding_modified_1_out_2, shifter_1_out, Zero_Handler_out_3;
  wire [16:0] multiplexer_2_out, multiplexer_3_out, right_shifter_1_out_4, significand_builder_1_out_3,
       significand_builder_2_out_3;

  Significand_Builder significand_builder_1 (.in_1(in_1[10:0]), .in_2(in_1[15]), .out_3(significand_builder_1_out_3));
  Subtractor #(.width(4)) subtractor_1 (
    .a(in_1[14:11]), .b(in_2[14:11]), .out(subtractor_1_out), .bin(1'b0), .bout(subtractor_1_bout));
  Multiplexer #(.width(4), .enable("false")) multiplexer_1 (
    .in0(in_1[14:11]), .in1(in_2[14:11]), .out(multiplexer_1_out), .sel(subtractor_1_bout));
  Significand_Builder significand_builder_2 (.in_1(in_2[10:0]), .in_2(in_2[15]), .out_3(significand_builder_2_out_3));
  Multiplexer #(.width(17), .enable("false")) multiplexer_2 (
    .in0(significand_builder_2_out_3), .in1(significand_builder_1_out_3), .out(multiplexer_2_out),
    .sel(subtractor_1_bout));
  Right_Shifter right_shifter_1 (
    .in_2(subtractor_1_out), .in_3(subtractor_1_bout), .in_1(multiplexer_2_out), .out_4(right_shifter_1_out_4));
  Adder_preprocessor Adder_preprocessor (.in_1(right_shifter_1_out_4), .out_2(Adder_preprocessor_out_2));
  Multiplexer #(.width(17), .enable("false")) multiplexer_3 (
    .in0(significand_builder_1_out_3), .in1(significand_builder_2_out_3), .out(multiplexer_3_out),
    .sel(subtractor_1_bout));
  Zero_handler Zero_Handler (.in_1(in_1), .in_2(in_2), .out_3(Zero_Handler_out_3), .out_4(Zero_Handler_out_4));
  Adder_preprocessor Adder_preprocessor_2 (.in_1(multiplexer_3_out), .out_2(Adder_preprocessor_2_out_2));
  Adder #(.width(16)) adder_1 (
    .a(Adder_preprocessor_2_out_2), .b(Adder_preprocessor_out_2), .out(adder_1_out), .cin(1'b0));  // open: cout
  assign not_1_out = ~adder_1_out;  // NOT_Gate not_1, 16 bits wide
  Adder #(.width(16)) adder_2 (.a(not_1_out), .b({16{1'b0}}), .out(adder_2_out), .cin(1'b1));  // open: cout
  Multiplexer #(.width(16), .enable("false")) multiplexer_4 (
    .in0(adder_1_out), .in1(adder_2_out), .out(multiplexer_4_out), .sel(adder_1_out[15]));
  Shifter #(.width(16)) shifter_1 (.in(multiplexer_4_out), .\dist (4'b0001), .out(shifter_1_out));
  normalize_sum normalize_sum_1 (
    .in_1(shifter_1_out), .in_2(multiplexer_1_out), .out_3(normalize_sum_1_out_3),
    .exponent(normalize_sum_1_exponent), .out_5(normalize_sum_1_out_5));
  rounding_modified rounding_modified_1 (.in_1(normalize_sum_1_out_3), .out_2(rounding_modified_1_out_2));
  normalize_sum normalize_sum_2 (
    .in_1(rounding_modified_1_out_2), .in_2(normalize_sum_1_exponent), .out_3(normalize_sum_2_out_3),
    .exponent(normalize_sum_2_exponent), .out_5(normalize_sum_2_out_5));
  Overflow_Underflow_Handler Overflow_Underflow_Handler (
    .in_1(normalize_sum_2_out_3), .in_2(normalize_sum_2_exponent), .in_3(normalize_sum_2_out_5),
    .in_4(normalize_sum_1_out_5), .in_5(adder_1_out[15]), .out_6(Overflow_Underflow_Handler_out_6),
    .overflow(Overflow_Underflow_Handler_overflow), .underflow(Overflow_Underflow_Handler_underflow));
  Multiplexer #(.width(16), .enable("false")) multiplexer_5 (
    .in0(Zero_Handler_out_3), .in1(Overflow_Underflow_Handler_out_6), .out(Answer), .sel(Zero_Handler_out_4));
  and and_1 (Overflow, Zero_Handler_out_4, Overflow_Underflow_Handler_overflow);
  and and_2 (Underflow, Zero_Handler_out_4, Overflow_Underflow_Handler_underflow);

  // Notes on the sheet:
  //   Exp subtractor
  //   exponent
  //   16 bit output, lowest 15 bit is ans
  //   left shift the 13 bit ans
  //   normalize_sum
  //   16 bit output, input of the rounding portion
  //   rounding
  //   exponent
  //   normalize_sum
  //   exponent_sign
  //   Output sign bit
endmodule

module normalize_sum (
  input  [15:0] in_1,
  input  [3:0] in_2,
  output [15:0] out_3,
  output [3:0] exponent,
  output out_5
);

  wire adder_1_cout, or_1_out, subtractor_1_bout;
  wire [3:0] adder_1_out, bit_extender_1_out, multiplexer_1_out, priority_encoder_1_out_2, subtractor_1_out;
  wire [15:0] shifter_1_out, shifter_2_out;

  priority_encoder priority_encoder_1 (.in_1(in_1[13:0]), .out_2(priority_encoder_1_out_2));
  or or_1 (or_1_out, priority_encoder_1_out_2[3], priority_encoder_1_out_2[2], priority_encoder_1_out_2[1], priority_encoder_1_out_2[0]);
  Shifter #(.width(16), .shift("lr")) shifter_1 (.in(in_1), .\dist (4'b0001), .out(shifter_1_out));
  Shifter #(.width(16)) shifter_2 (.in(in_1), .\dist (priority_encoder_1_out_2), .out(shifter_2_out));
  Multiplexer #(.width(4), .enable("false")) multiplexer_1 (
    .in0(in_2), .in1(priority_encoder_1_out_2), .out(multiplexer_1_out), .sel(or_1_out));
  Multiplexer #(.select(2), .width(16), .enable("false")) multiplexer_2 (
    .in0(shifter_2_out), .in1(in_1), .in2(shifter_1_out), .in3(shifter_1_out), .out(out_3), .sel(in_1[15:14]));
  assign bit_extender_1_out = {{3{1'b0}}, in_1[15]};  // Bit_Extender bit_extender_1
  Subtractor #(.width(4)) subtractor_1 (
    .a(in_2), .b(multiplexer_1_out), .out(subtractor_1_out), .bin(1'b0), .bout(subtractor_1_bout));
  Adder #(.width(4)) adder_1 (.a(bit_extender_1_out), .b(in_2), .out(adder_1_out), .cin(1'b0), .cout(adder_1_cout));
  Multiplexer #(.select(2), .width(4), .enable("false")) multiplexer_3 (
    .in0(subtractor_1_out), .in1(adder_1_out), .in2(adder_1_out), .in3(adder_1_out), .out(exponent),
    .sel(in_1[15:14]));
  Multiplexer #(.select(2), .enable("false")) multiplexer_4 (
    .in0(subtractor_1_bout), .in1(adder_1_cout), .in2(adder_1_cout), .in3(adder_1_cout), .out(out_5),
    .sel(in_1[15:14]));

  // Notes on the sheet:
  //   Big ALU result shifted
  //   exponent
  //   determine left shift amount
  //   Priority_encoder
  //   shamt
  //   result_all_0's?
  //   shifting_result
  //   exp_sub
  //   exp_inc
  //   normalize_frac
  //   exp_sign
endmodule

module priority_encoder (
  input  [13:0] in_1,
  output [3:0] out_2
);

  wire or_1_out, or_2_out;
  wire [2:0] not_1_out, priority_encoder_1_out, priority_encoder_2_out;
  wire [3:0] adder_1_out, adder_2_out, adder_3_out, bit_extender_1_out, bit_extender_2_out,
       multiplexer_1_out, not_2_out;

  Priority_Encoder priority_encoder_1 (
    .in0(1'b1), .in1(in_1[0]), .in2(in_1[1]), .in3(in_1[2]), .in4(in_1[3]), .in5(in_1[4]), .in6(in_1[5]),
    .in7(in_1[6]), .out(priority_encoder_1_out));  // open: en_in, gs, en_out
  Priority_Encoder priority_encoder_2 (
    .in0(1'b1), .in1(in_1[7]), .in2(in_1[8]), .in3(in_1[9]), .in4(in_1[10]), .in5(in_1[11]), .in6(in_1[12]),
    .in7(in_1[13]), .out(priority_encoder_2_out));  // open: en_in, gs, en_out
  assign bit_extender_1_out = {{1{1'b0}}, priority_encoder_1_out};  // Bit_Extender bit_extender_1
  assign bit_extender_2_out = {{1{1'b0}}, not_1_out};  // Bit_Extender bit_extender_2
  assign not_1_out = ~priority_encoder_2_out;  // NOT_Gate not_1, 3 bits wide
  or or_1 (or_1_out, priority_encoder_2_out[2], priority_encoder_2_out[1], priority_encoder_2_out[0]);
  or or_2 (or_2_out, priority_encoder_1_out[0], priority_encoder_1_out[1], priority_encoder_1_out[2]);
  assign not_2_out = ~bit_extender_1_out;  // NOT_Gate not_2, 4 bits wide
  Adder #(.width(4)) adder_1 (.a(not_2_out), .b(4'b0001), .out(adder_1_out));  // open: cin, cout
  Adder #(.width(4)) adder_2 (.a(bit_extender_2_out), .b(4'b0001), .out(adder_2_out));  // open: cin, cout
  Adder #(.width(4)) adder_3 (.a(4'b1111), .b(adder_1_out), .out(adder_3_out));  // open: cin, cout
  Multiplexer #(.width(4), .enable("false")) multiplexer_1 (
    .in0(bit_extender_1_out), .in1(adder_3_out), .out(multiplexer_1_out), .sel(or_2_out));
  Multiplexer #(.width(4), .enable("false")) multiplexer_2 (
    .in0(multiplexer_1_out), .in1(adder_2_out), .out(out_2), .sel(or_1_out));

  // Notes on the sheet:
  //   LSB
  //   MSB
endmodule

module rounding_modified (
  input  [15:0] in_1,
  output [15:0] out_2
);

  wire or_1_out;
  wire [0:0] and_1_out;

  or or_1 (or_1_out, in_1[0], in_1[1], in_1[3]);
  and and_1 (and_1_out[0], or_1_out, in_1[2]);
  Adder #(.width(13)) adder_1 (.a({{12{1'b0}}, and_1_out[0]}), .b(in_1[15:3]), .out(out_2[15:3]));  // open: cin, cout

  assign out_2[2:0] = 3'b000;
endmodule

module Zero_handler (
  input  [15:0] in_1,
  input  [15:0] in_2,
  output [15:0] out_3,
  output out_4
);

  wire [1:0] or_1_out;

  or or_1 (or_1_out[0], in_1[0], in_1[1], in_1[2], in_1[3], in_1[4], in_1[5], in_1[6], in_1[7], in_1[8], in_1[9], in_1[10], in_1[11], in_1[12], in_1[13], in_1[14]);
  or or_2 (or_1_out[1], in_2[0], in_2[1], in_2[2], in_2[3], in_2[4], in_2[5], in_2[6], in_2[7], in_2[8], in_2[9], in_2[10], in_2[11], in_2[12], in_2[13], in_2[14]);
  Multiplexer #(.select(2), .width(16), .enable("false")) multiplexer_1 (
    .in0({16{1'b0}}), .in1(in_1), .in2(in_2), .in3({16{1'b0}}), .out(out_3), .sel(or_1_out));
  and and_1 (out_4, or_1_out[0], or_1_out[1]);
endmodule

module Overflow_Underflow_Handler (
  input  [15:0] in_1,
  input  [3:0] in_2,
  input  in_3,
  input  in_4,
  input  in_5,
  output [15:0] out_6,
  output overflow,
  output underflow
);

  wire and_1_out, nor_1_out, not_1_out, or_1_out, or_2_out, or_3_out;

  or or_1 (or_1_out, in_3, in_4);
  or or_2 (or_2_out, in_1[14], in_2[0], in_2[1], in_2[2], in_2[3]);
  and and_1 (and_1_out, in_2[0], in_2[1], in_2[2], in_2[3]);
  and and_2 (overflow, and_1_out, not_1_out);
  not not_1 (not_1_out, or_1_out);
  nor nor_1 (nor_1_out, in_2[0], in_2[1], in_2[2], in_2[3]);
  or or_3 (or_3_out, nor_1_out, or_1_out);
  and and_3 (underflow, or_3_out, or_2_out);

  assign out_6 = {in_5, in_2, in_1[13:3]};

  // Notes on the sheet:
  //   Normalized sum
  //   exponent
  //   Output sign bit
  //   exponent_sign
endmodule
